# Fritzing sketch labs (saved by Fritzing 0.9.3b)
circuit board: 8.46667cm x 5.64444cm
breadboards: 2

parts:
  Raspberry_Pi_4 = Raspberry Pi 3 [part_number=RPI-3-V1.2]
  J6 = T Cobbler Plus
  LED10 = LED - 5mm [color="Red (633nm)" current=20 package="5 mm [THT]"]
  LED11 = LED - 5mm [color="Yellow (595nm)" package="5 mm [THT]"]
  LED12 = LED - 5mm [color="Green (555nm)" package="5 mm [THT]"]
  Raspberry_Pi_5 = Raspberry Pi 3 [part_number=RPI-3-V1.2]
  J7 = T Cobbler Plus
  LED13 = LED - 5mm [color="Red (633nm)" current=20 package="5 mm [THT]"]
  LED14 = LED - 5mm [color="Yellow (595nm)" package="5 mm [THT]"]
  LED15 = LED - 5mm [color="Green (555nm)" package="5 mm [THT]"]
  S2 = Pushbutton [package="[THT]"]
  R2 = Resistor [tolerance=±5% resistance=8.2k package=THT]

nets:
  3V3: Raspberry_Pi_4.3v3, Raspberry_Pi_4.3V3, J6.3.3V#41, J6.3.3V#57
  N1: Raspberry_Pi_4.GPIO2, J6.GPIO_2
  N2: Raspberry_Pi_4.GPIO3, J6.GPIO_3
  N3: Raspberry_Pi_4.GPIO4, J6.GPIO_4
  N4: Raspberry_Pi_4.GND, J6.GND#46, J6.GND#49, J6.GND#54, J6.GND#60, J6.GND#65, J6.GND#70, J6.GND#74, J6.GND#79
  N5: Raspberry_Pi_4.GPIO17, J6.GPIO_17
  N6: Raspberry_Pi_4.GPIO27, J6.GPIO_27
  N7: Raspberry_Pi_4.GPIO22, J6.GPIO_22
  N8: Raspberry_Pi_4.GPIO10, J6.GPIO_10
  N9: Raspberry_Pi_4.GPIO9, J6.GPIO_9
  N10: Raspberry_Pi_4.GPIO11, J6.GPIO_11
  N11: Raspberry_Pi_4.ID_SD, J6.ID_SD
  N12: Raspberry_Pi_4.GPIO5, J6.GPIO_5
  N13: Raspberry_Pi_4.GPIO6, J6.GPIO_6
  N14: Raspberry_Pi_4.GPIO13, J6.GPIO_13
  N15: Raspberry_Pi_4.GPIO19, J6.GPIO_19
  N16: Raspberry_Pi_4.GPIO26, J6.GPIO_26
  N17: Raspberry_Pi_4.GPIO21, J6.GPIO_21
  N18: Raspberry_Pi_4.GPIO20, J6.GPIO_20
  N19: Raspberry_Pi_4.GPIO16, J6.GPIO_16
  N20: Raspberry_Pi_4.GPIO12, J6.GPIO_12
  N21: Raspberry_Pi_4.ID_SC, J6.ID_SC
  N22: Raspberry_Pi_4.GPIO7, J6.GPIO_7
  N23: Raspberry_Pi_4.GPIO8, J6.GPIO_8
  N24: Raspberry_Pi_4.GPIO25, J6.GPIO_25
  N25: Raspberry_Pi_4.GPIO24, J6.GPIO_24
  N26: Raspberry_Pi_4.GPIO23, J6.GPIO_23
  N27: Raspberry_Pi_4.GPIO18, J6.GPIO_18
  N28: Raspberry_Pi_4.GPIO15, J6.GPIO_15
  N29: Raspberry_Pi_4.GPIO14, J6.GPIO_14
  5V: Raspberry_Pi_4.5V, J6.5V
  N30: J6.#13, LED10.anode
  N31: J6.#19, LED11.anode
  N32: J6.#26, LED12.anode
  N33: J6.GND#38, LED10.cathode, LED11.cathode, LED12.cathode
  3V3_2: Raspberry_Pi_5.3v3, Raspberry_Pi_5.3V3, J7.3.3V#41, J7.3.3V#57
  N34: Raspberry_Pi_5.GPIO2, J7.GPIO_2
  N35: Raspberry_Pi_5.GPIO3, J7.GPIO_3
  N36: Raspberry_Pi_5.GPIO4, J7.GPIO_4
  N37: Raspberry_Pi_5.GND, J7.GND#46, J7.GND#49, J7.GND#54, J7.GND#60, J7.GND#65, J7.GND#70, J7.GND#74, J7.GND#79
  N38: Raspberry_Pi_5.GPIO17, J7.GPIO_17
  N39: Raspberry_Pi_5.GPIO27, J7.GPIO_27
  N40: Raspberry_Pi_5.GPIO22, J7.GPIO_22
  N41: Raspberry_Pi_5.GPIO10, J7.GPIO_10
  N42: Raspberry_Pi_5.GPIO9, J7.GPIO_9
  N43: Raspberry_Pi_5.GPIO11, J7.GPIO_11
  N44: Raspberry_Pi_5.ID_SD, J7.ID_SD
  N45: Raspberry_Pi_5.GPIO5, J7.GPIO_5
  N46: Raspberry_Pi_5.GPIO6, J7.GPIO_6
  N47: Raspberry_Pi_5.GPIO13, J7.GPIO_13
  N48: Raspberry_Pi_5.GPIO19, J7.GPIO_19
  N49: Raspberry_Pi_5.GPIO26, J7.GPIO_26
  N50: Raspberry_Pi_5.GPIO21, J7.GPIO_21
  N51: Raspberry_Pi_5.GPIO20, J7.GPIO_20
  N52: Raspberry_Pi_5.GPIO16, J7.GPIO_16
  N53: Raspberry_Pi_5.GPIO12, J7.GPIO_12
  N54: Raspberry_Pi_5.ID_SC, J7.ID_SC
  N55: Raspberry_Pi_5.GPIO7, J7.GPIO_7
  N56: Raspberry_Pi_5.GPIO8, J7.GPIO_8
  N57: Raspberry_Pi_5.GPIO25, J7.GPIO_25
  N58: Raspberry_Pi_5.GPIO24, J7.GPIO_24
  N59: Raspberry_Pi_5.GPIO23, J7.GPIO_23
  N60: Raspberry_Pi_5.GPIO18, J7.GPIO_18
  N61: Raspberry_Pi_5.GPIO15, J7.GPIO_15
  N62: Raspberry_Pi_5.GPIO14, J7.GPIO_14
  5V_2: Raspberry_Pi_5.5V, J7.5V
  N63: J7.3V3, S2.Pin_1, S2.Pin_2
  N64: J7.#13, LED13.anode
  N65: J7.#19, LED14.anode
  N66: J7.#26, LED15.anode
  N67: J7.GND#38, LED13.cathode, LED14.cathode, LED15.cathode, R2.Pin_1
  N68: J7.#21, S2.Pin_3, S2.Pin_4, R2.Pin_0

custom parts:
  T Cobbler Plus: The T-Cobbler Plus is an add on prototyping board from Adafruit specifically designed for the Raspberry Pi B+ that can break out all those tasty power, GPIO, I2C and SPI pins from the 40-pin header onto a solderless breadboard. This set will make "cobbling together" prototypes with the Pi super easy. The T-Cobbler Plus can plug into any solderless breadboard.
